# Fritzing sketch project_02 (saved by Fritzing 0.9.1b)
breadboards: 1

parts:
  S1 = Pushbutton [package="[THT]"]
  R1 = Resistor [tolerance=±5% resistance=220 package=THT]
  R2 = Resistor [tolerance=±5% resistance=220 package=THT]
  R3 = Resistor [tolerance=±5% resistance=220 package=THT]
  R4 = Resistor [tolerance=±5% resistance=10k package=THT]
  LED2 = LED - 5mm [color="Red (633nm)" package="5 mm [THT]"]
  LED3 = smd LED [color="Green (555nm)" package="1206 [SMD]"]
  LED4 = LED - 5mm [color="Red (633nm)" package="5 mm [THT]"]
  Part1 = Arduino Uno (Rev3)

nets:
  N1: S1.Pin_1, S1.Pin_2, R4.Pin_0, Part1.D2
  N2: S1.Pin_3, S1.Pin_4, Part1.5V
  N3: R1.Pin_0, R2.Pin_0, R3.Pin_0, R4.Pin_1, Part1.GND
  N4: R1.Pin_1, LED3.cathode
  N5: R2.Pin_1, LED4.cathode
  N6: R3.Pin_1, LED2.cathode
  N7: LED2.anode, Part1.D5_PWM
  N8: LED3.anode, Part1.D3_PWM
  N9: LED4.anode, Part1.D4
